// Logisim project control-logic.circ as structural Verilog: 1 circuit, main circuit control_logic
module control_logic (
  input  [31:0] Instruction,
  input  BrEq,
  input  BrLt,
  output PCSel,
  output RegWEn,
  output [2:0] ImmSel,
  output BrUn,
  output ASel,
  output BSel,
  output [3:0] ALUSel,
  output MemWEn,
  output [1:0] WBSel,
  output out_13,
  output out_14,
  output out_15,
  output out_16,
  output out_17
);

  wire and_7_out, and_8_out, and_9_out, and_10_out, and_11_out, and_12_out, and_13_out, comparator_1_eq,
       comparator_2_eq, comparator_3_eq, comparator_4_eq, comparator_5_eq, comparator_6_eq, comparator_7_eq,
       comparator_8_eq, comparator_9_eq, comparator_10_eq, comparator_11_eq, comparator_12_eq,
       comparator_13_eq, comparator_14_eq, comparator_15_eq, comparator_16_eq, comparator_17_eq,
       comparator_18_eq, comparator_19_eq, comparator_22_eq, comparator_23_eq, comparator_24_eq,
       comparator_25_eq, comparator_26_eq, comparator_27_eq, comparator_28_eq, comparator_29_eq,
       comparator_30_eq, comparator_31_eq, comparator_32_eq, comparator_33_eq, comparator_34_eq,
       comparator_35_eq, comparator_36_eq, comparator_37_eq, comparator_38_eq, comparator_39_eq,
       comparator_40_eq, comparator_41_eq, comparator_42_eq, comparator_43_eq, comparator_44_eq,
       comparator_45_eq, comparator_46_eq, comparator_47_eq, ImmSelSB, ImmSelU, isAnd, isOr, isSll, isSlt,
       isSrai, isSrl, isSub, isXor, Itype, not_1_out, not_2_out, not_3_out, or_2_out, or_3_out, or_9_out,
       or_10_out, Rtype, WBSelALUout;
  wire [2:0] multiplexer_5_out;
  wire [3:0] bit_extender_1_out, multiplexer_2_out, multiplexer_3_out, multiplexer_4_out, multiplexer_6_out,
       multiplexer_7_out, multiplexer_9_out, multiplexer_10_out, multiplexer_11_out;

  Comparator #(.width(7)) comparator_1 (.a(Instruction[6:0]), .b(7'b0010011), .eq(comparator_1_eq));  // open: gt, lt
  Comparator #(.width(7)) comparator_2 (.a(Instruction[6:0]), .b(7'b0000011), .eq(comparator_2_eq));  // open: gt, lt
  Comparator #(.width(7)) comparator_3 (.a(Instruction[6:0]), .b(7'b1100111), .eq(comparator_3_eq));  // open: gt, lt
  Comparator #(.width(7)) comparator_4 (.a(Instruction[6:0]), .b(7'b0110011), .eq(comparator_4_eq));  // open: gt, lt
  Comparator #(.width(7)) comparator_5 (.a(Instruction[6:0]), .b(7'b1101111), .eq(comparator_5_eq));  // open: gt, lt
  Comparator #(.width(7)) comparator_6 (.a(Instruction[6:0]), .b(7'b0110111), .eq(comparator_6_eq));  // open: gt, lt
  Comparator #(.width(7)) comparator_7 (.a(Instruction[6:0]), .b(7'b0010111), .eq(comparator_7_eq));  // open: gt, lt
  Comparator #(.width(7)) comparator_8 (.a(Instruction[6:0]), .b(7'b1100111), .eq(comparator_8_eq));  // open: gt, lt
  Comparator #(.width(7)) comparator_9 (.a(Instruction[6:0]), .b(7'b0110011), .eq(comparator_9_eq));  // open: gt, lt
  Comparator #(.width(7)) comparator_10 (.a(Instruction[6:0]), .b(7'b0010011), .eq(comparator_10_eq));  // open: gt, lt
  Comparator #(.width(7)) comparator_11 (.a(Instruction[6:0]), .b(7'b0000011), .eq(comparator_11_eq));  // open: gt, lt
  or or_1 (Itype, comparator_1_eq, comparator_2_eq, comparator_3_eq);
  and and_1 (Rtype, comparator_4_eq, 1'b1);
  or or_2 (or_2_out, comparator_5_eq, comparator_6_eq, comparator_7_eq);
  or or_3 (or_3_out, comparator_9_eq, comparator_10_eq, comparator_11_eq);
  or or_4 (RegWEn, or_2_out, comparator_8_eq, or_3_out);
  Comparator #(.width(3)) comparator_12 (.a(Instruction[14:12]), .b(3'b000), .eq(comparator_12_eq));  // open: gt, lt
  Comparator #(.width(3)) comparator_13 (.a(Instruction[14:12]), .b(3'b001), .eq(comparator_13_eq));  // open: gt, lt
  Multiplexer #(.width(2)) multiplexer_1 (.in0(2'b00), .in1(2'b01), .out(WBSel), .sel(WBSelALUout));
  Comparator #(.width(3)) comparator_14 (.a(Instruction[14:12]), .b(3'b010), .eq(comparator_14_eq));  // open: gt, lt
  Comparator #(.width(3)) comparator_15 (.a(Instruction[14:12]), .b(3'b100), .eq(comparator_15_eq));  // open: gt, lt
  Comparator #(.width(3)) comparator_16 (.a(Instruction[14:12]), .b(3'b101), .eq(comparator_16_eq));  // open: gt, lt
  Comparator #(.width(7)) comparator_17 (.a(Instruction[6:0]), .b(7'b0010111), .eq(comparator_17_eq));  // open: gt, lt
  Comparator #(.width(7)) comparator_18 (.a(Instruction[6:0]), .b(7'b0110011), .eq(comparator_18_eq));  // open: gt, lt
  Comparator #(.width(7)) comparator_19 (.a(Instruction[6:0]), .b(7'b0010011), .eq(comparator_19_eq));  // open: gt, lt
  and and_2 (out_13, comparator_2_eq, comparator_12_eq);
  and and_3 (out_14, comparator_2_eq, comparator_13_eq);
  and and_4 (out_15, comparator_2_eq, comparator_14_eq);
  and and_5 (out_16, comparator_2_eq, comparator_15_eq);
  and and_6 (out_17, comparator_2_eq, comparator_16_eq);
  or or_5 (WBSelALUout, comparator_17_eq, comparator_18_eq, comparator_19_eq);
  Comparator #(.width(7)) comparator_20 (.a(Instruction[6:0]), .b(7'b0100011), .eq(MemWEn));  // open: gt, lt
  not not_1 (not_1_out, BrLt);
  Comparator #(.width(7)) comparator_21 (.a(Instruction[6:0]), .b(7'b1100011), .eq(ImmSelSB));  // open: gt, lt
  Comparator #(.width(3)) comparator_22 (.a(Instruction[14:12]), .b(3'b000), .eq(comparator_22_eq));  // open: gt, lt
  Comparator #(.width(3)) comparator_23 (.a(Instruction[14:12]), .b(3'b101), .eq(comparator_23_eq));  // open: gt, lt
  Comparator #(.width(3)) comparator_24 (.a(Instruction[14:12]), .b(3'b111), .eq(comparator_24_eq));  // open: gt, lt
  Comparator #(.width(3)) comparator_25 (.a(Instruction[14:12]), .b(3'b100), .eq(comparator_25_eq));  // open: gt, lt
  Comparator #(.width(3)) comparator_26 (.a(Instruction[14:12]), .b(3'b110), .eq(comparator_26_eq));  // open: gt, lt
  not not_2 (not_2_out, BrEq);
  Comparator #(.width(3)) comparator_27 (.a(Instruction[14:12]), .b(3'b001), .eq(comparator_27_eq));  // open: gt, lt
  and and_7 (and_7_out, Itype, 1'b1);
  Comparator #(.width(7)) comparator_28 (.a(Instruction[6:0]), .b(7'b1100011), .eq(comparator_28_eq));  // open: gt, lt
  Comparator #(.width(7)) comparator_29 (.a(Instruction[6:0]), .b(7'b0010111), .eq(comparator_29_eq));  // open: gt, lt
  Comparator #(.width(7)) comparator_30 (.a(Instruction[6:0]), .b(7'b0110111), .eq(comparator_30_eq));  // open: gt, lt
  Comparator #(.width(7)) comparator_31 (.a(Instruction[6:0]), .b(7'b1101111), .eq(comparator_31_eq));  // open: gt, lt
  and and_8 (and_8_out, ImmSelSB, BrEq, comparator_22_eq);
  and and_9 (and_9_out, ImmSelSB, not_1_out, comparator_23_eq);
  not not_3 (not_3_out, ImmSelSB);
  and and_10 (and_10_out, ImmSelSB, BrLt, comparator_25_eq);
  and and_11 (and_11_out, ImmSelSB, BrLt, comparator_26_eq);
  and and_12 (and_12_out, ImmSelSB, not_2_out, comparator_27_eq);
  Comparator #(.width(7)) comparator_32 (.a(Instruction[6:0]), .b(7'b0010111), .eq(comparator_32_eq));  // open: gt, lt
  Comparator #(.width(7)) comparator_33 (.a(Instruction[6:0]), .b(7'b1101111), .eq(comparator_33_eq));  // open: gt, lt
  and and_13 (and_13_out, ImmSelSB, not_3_out, comparator_24_eq);
  or or_6 (BSel, and_7_out, comparator_28_eq, comparator_29_eq, comparator_30_eq, comparator_31_eq);
  or or_7 (PCSel, and_8_out, and_9_out, and_13_out, and_10_out, and_11_out, and_12_out);
  or or_8 (ASel, ImmSelSB, comparator_32_eq, comparator_33_eq);
  Comparator #(.width(3)) comparator_34 (.a(Instruction[14:12]), .b(3'b111), .eq(comparator_34_eq));  // open: gt, lt
  Comparator #(.width(3)) comparator_35 (.a(Instruction[14:12]), .b(3'b110), .eq(comparator_35_eq));  // open: gt, lt
  or or_9 (or_9_out, comparator_34_eq, comparator_35_eq);
  and and_14 (BrUn, ImmSelSB, or_9_out);
  Comparator #(.width(7)) comparator_36 (.a(Instruction[31:25]), .b({7{1'b0}}), .eq(comparator_36_eq));  // open: gt, lt
  assign bit_extender_1_out = {{1{1'b0}}, Instruction[14:12]};  // Bit_Extender bit_extender_1
  Multiplexer #(.width(4)) multiplexer_2 (
    .in0(4'b0000), .in1(bit_extender_1_out), .out(multiplexer_2_out), .sel(or_10_out));
  or or_10 (or_10_out, 1'b0, Itype);
  Comparator #(.width(3)) comparator_37 (.a(Instruction[14:12]), .b(3'b111), .eq(comparator_37_eq));  // open: gt, lt
  Comparator #(.width(3)) comparator_38 (.a(Instruction[14:12]), .b(3'b110), .eq(comparator_38_eq));  // open: gt, lt
  Comparator #(.width(3)) comparator_39 (.a(Instruction[14:12]), .b(3'b100), .eq(comparator_39_eq));  // open: gt, lt
  Comparator #(.width(3)) comparator_40 (.a(Instruction[14:12]), .b(3'b001), .eq(comparator_40_eq));  // open: gt, lt
  Comparator #(.width(3)) comparator_41 (.a(Instruction[14:12]), .b(3'b101), .eq(comparator_41_eq));  // open: gt, lt
  Comparator #(.width(3)) comparator_42 (.a(Instruction[14:12]), .b(3'b010), .eq(comparator_42_eq));  // open: gt, lt
  Multiplexer #(.width(4)) multiplexer_3 (
    .in0(multiplexer_2_out), .in1(4'b1101), .out(multiplexer_3_out), .sel(isSrai));
  Comparator #(.width(7)) comparator_43 (.a(Instruction[6:0]), .b(7'b0010111), .eq(comparator_43_eq));  // open: gt, lt
  Comparator #(.width(7)) comparator_44 (.a(Instruction[6:0]), .b(7'b0110111), .eq(comparator_44_eq));  // open: gt, lt
  and and_15 (isAnd, Rtype, comparator_36_eq, comparator_37_eq);
  and and_16 (isOr, Rtype, comparator_36_eq, comparator_38_eq);
  and and_17 (isXor, Rtype, comparator_36_eq, comparator_39_eq);
  and and_18 (isSll, Rtype, comparator_36_eq, comparator_40_eq);
  and and_19 (isSrl, Rtype, comparator_36_eq, comparator_41_eq);
  and and_20 (isSlt, Rtype, comparator_36_eq, comparator_42_eq);
  Multiplexer #(.width(4)) multiplexer_4 (.in0(multiplexer_3_out), .in1(4'b1100), .out(multiplexer_4_out), .sel(isSub));
  Multiplexer #(.width(3)) multiplexer_5 (.in0(3'b000), .in1(3'b010), .out(multiplexer_5_out), .sel(ImmSelSB));
  Multiplexer #(.width(4)) multiplexer_6 (.in0(multiplexer_4_out), .in1(4'b0111), .out(multiplexer_6_out), .sel(isAnd));
  or or_11 (ImmSelU, comparator_43_eq, comparator_44_eq);
  Multiplexer #(.width(4)) multiplexer_7 (.in0(multiplexer_6_out), .in1(4'b0110), .out(multiplexer_7_out), .sel(isOr));
  Multiplexer #(.width(3)) multiplexer_8 (.in0(multiplexer_5_out), .in1(3'b011), .out(ImmSel), .sel(ImmSelU));
  Multiplexer #(.width(4)) multiplexer_9 (.in0(multiplexer_7_out), .in1(4'b0100), .out(multiplexer_9_out), .sel(isXor));
  Comparator #(.width(3)) comparator_45 (.a(Instruction[14:12]), .b(3'b101), .eq(comparator_45_eq));  // open: gt, lt
  Comparator #(.width(7)) comparator_46 (
    .a(Instruction[31:25]), .b(7'b0100000), .eq(comparator_46_eq));  // open: gt, lt
  Comparator #(.width(3)) comparator_47 (.a(Instruction[14:12]), .b(3'b000), .eq(comparator_47_eq));  // open: gt, lt
  Multiplexer #(.width(4)) multiplexer_10 (
    .in0(multiplexer_9_out), .in1(4'b0001), .out(multiplexer_10_out), .sel(isSll));
  and and_21 (isSrai, Itype, comparator_45_eq, comparator_46_eq);
  Multiplexer #(.width(4)) multiplexer_11 (
    .in0(multiplexer_10_out), .in1(4'b0101), .out(multiplexer_11_out), .sel(isSrl));
  Multiplexer #(.width(4)) multiplexer_12 (.in0(multiplexer_11_out), .in1(4'b0010), .out(ALUSel), .sel(isSlt));
  and and_22 (isSub, comparator_46_eq, Rtype, comparator_47_eq);

  // Other names for the same wires on the sheet: opcode[6:0] = Instruction[6:0]; rd[4:0] = Instruction[11:7];
  //   func3[2:0] = Instruction[14:12]; rs1[4:0] = Instruction[19:15]; rs2[4:0] = Instruction[24:20];
  //   func7[6:0] = Instruction[31:25]; lb = out_13; lbu = out_16; lh = out_14; lhu = out_17; lw = out_15

  // Notes on the sheet:
  //   INPUTS to your circuit
  //   jal
  //   lui
  //   auipc
  //   jalr
  //   R
  //   I
  //   load
  //   DON'T CHANGE THE LOCATIONS OF THE INPUTS AND OUTPUTS!
  //   lw
  //   lbu
  //   lhu
  //   R
  //   I
  //   OUTPUT from your circuit
  //   | 0b0000011 | lb, lh, lw, ld, lbu, lhu, lwu 
  //   lb
  //   lh
  //   Instruction Decode
  //   BSel is 1 for any of the following opcodes
  //   | 0b1100111 | jalr 
  //   | 0b0010111 | auipc 
  //   | 0b0110111 | lui
  //   | 0b1101111 | jal
  //   B operand is immediate
  //   | 0b0010011 | addi, slli, xori, srli, srai, ori, andi
  //   | 0b0000011 | lb, lh, lw, ld, lbu, lhu, lwu
  //   | 0b1100011 | beq, bne, blt, bge, bltu, bgeu
  //   beq
  //   bge
  //   bgeu
  //   blt
  //   bltu
  //   bne
  //   Select a program counter reference to use for the A Operand
  //   Sign extend if true (srai)
  //   This should pass the value 13 to the alu if we're dealing with srai
endmodule
